# Fritzing sketch AnnaButtonRGB (saved by Fritzing 0.9.3b)
breadboards: 1

parts:
  U1 = NodeMCU V1.0
  LED1 = RGB LED (com. cathode, rgb) [package="5 mm [THT]"]
  R1 = Resistor [tolerance=±5% resistance=220 package=THT]
  R2 = Resistor [tolerance=±5% resistance=220 package=THT]
  R3 = Resistor [tolerance=±5% resistance=220 package=THT]
  S1 = Pushbutton [package="[THT]"]
  J1 = Piezo Speaker  # not connected

nets:
  N1: U1.D0, R3.Pin_1, S1.Pin_1, S1.Pin_2
  N2: U1.D1, LED1.red_anode, R1.Pin_0, R1.Pin_1
  N3: U1.D2, LED1.common_cathode, R2.Pin_1
  N4: U1.3V3, LED1.green_anode, LED1.blue_anode, S1.Pin_3, S1.Pin_4
  N5: U1.GND, R3.Pin_0

custom parts:
  NodeMCU V1.0: ESP8266 based NodeMCU
